// Logisim project lista.circ as structural Verilog: 5 circuits, main circuit main
module main (
  input  A,
  input  B,
  output s0,
  output s1,
  output s2,
  output s3
);

  wire NOT_2_out, NOT_3_out, NOT_4_out, NOT_out;

  not NOT (NOT_out, B);
  not NOT_2 (NOT_2_out, A);
  not NOT_3 (NOT_3_out, B);
  not NOT_4 (NOT_4_out, A);
  and AND (s0, NOT_out, NOT_2_out);
  and AND_2 (s1, NOT_3_out, A);
  and AND_3 (s2, B, NOT_4_out);
  and AND_4 (s3, B, A);
endmodule

module \_2bits_de_entrada_e_4_saídas  (
  input  A,
  input  B,
  output s0,
  output s1,
  output s2,
  output s3
);

  wire NOT_2_out, NOT_3_out, NOT_4_out, NOT_out;

  not NOT (NOT_out, B);
  not NOT_2 (NOT_2_out, A);
  not NOT_3 (NOT_3_out, B);
  not NOT_4 (NOT_4_out, A);
  and AND (s0, NOT_out, NOT_2_out);
  and AND_2 (s1, NOT_3_out, A);
  and AND_3 (s2, B, NOT_4_out);
  and AND_4 (s3, B, A);
endmodule

module \_3bits_de_entrada_e_8_saídas  (
  input  A,
  input  B,
  input  C,
  output s0,
  output s1,
  output s2,
  output s3,
  output s4,
  output s5,
  output s6,
  output s7
);

  wire not_1_out, not_2_out, not_3_out, not_4_out, not_5_out, not_6_out, not_7_out, not_8_out, not_9_out,
       not_10_out, not_11_out, not_12_out;

  not not_1 (not_1_out, C);
  not not_2 (not_2_out, B);
  not not_3 (not_3_out, A);
  not not_4 (not_4_out, A);
  not not_5 (not_5_out, B);
  not not_6 (not_6_out, A);
  not not_7 (not_7_out, C);
  not not_8 (not_8_out, A);
  not not_9 (not_9_out, B);
  not not_10 (not_10_out, C);
  not not_11 (not_11_out, B);
  not not_12 (not_12_out, C);
  and AND (s0, not_1_out, not_2_out, not_3_out);
  and AND_2 (s1, not_4_out, not_5_out, C);
  and AND_3 (s2, not_6_out, B, not_7_out);
  and AND_4 (s3, not_8_out, B, C);
  and AND_5 (s4, A, not_9_out, not_10_out);
  and AND_6 (s5, A, not_11_out, C);
  and AND_7 (s6, A, B, not_12_out);
  and AND_8 (s7, C, B, A);
endmodule

module \_2bits_de_entrada_e_4saídas_com_o_logisim  (
  input  [1:0] a,
  output s0,
  output s1,
  output s2,
  output s3
);

  Decoder #(.select(2)) decoder_1 (.out0(s0), .out1(s1), .out2(s2), .out3(s3), .sel(a));  // open: en
endmodule

module \_3bits_de_entrada_e_8saídas_logisim  (
  input  [2:0] A,
  output s7,
  output s6,
  output s5,
  output s4,
  output s3,
  output s2,
  output s1,
  output s0
);

  Decoder #(.select(3)) decoder_1 (
    .out0(s0), .out1(s1), .out2(s2), .out3(s3), .out4(s4), .out5(s5), .out6(s6), .out7(s7), .sel(A));  // open: en
endmodule
